# Fritzing sketch Fritzing Circuit(Using ESP8266) (saved by Fritzing 0.9.3b)
circuit board: 6.04741cm x 5.72064cm
breadboards: 1

parts:
  ESP8266 = ESP8266 NodeMCU LoLin module
  J = Piezo Speaker
  R = Resistor [tolerance=±5% resistance=220 package=THT]
  MPU = Adafruit MPU6050
  LED = LED - 5mm [color="Red (633nm)" package="5 mm [THT]"]
  S = Pushbutton [package="[THT]"]

nets:
  N1: ESP8266.D4, LED.anode
  3V3: ESP8266.3V3, MPU.VCC
  GND: ESP8266.GND, J.pin1, R.Pin_1, MPU.GND, S.Pin_1, S.Pin_2
  N2: ESP8266.D5, J.pin2
  N3: ESP8266.D6, S.Pin_3, S.Pin_4
  N4: ESP8266.D7, MPU.SCL
  N5: ESP8266.D8, MPU.SDA
  N6: R.Pin_0, LED.cathode

custom parts:
  ESP8266 NodeMCU LoLin module: ESP8266 based NodeMCU
  Adafruit MPU6050: The MPU-6050 is a popular six axis accelerometer and gyroscope (gyro) that has all the info you need on how things are shakin' and spinnin' . With six axes of sensing and 16-bit measurements, you'll have everything you need to give your robot friend an inner ear. This combination of gyroscopes and accelerometers is commonly referred to as an Inertial Measurement Unit or IMU. Not so long ago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
